# Fritzing sketch Scheme (saved by Fritzing 0.9.1b)

parts:
  Arduino1 = Arduino Uno (Rev3)
  Деталь1 = PWM Shield

nets:
  N1: Arduino1.D8, Деталь1.D8
  N2: Arduino1.D9_PWM, Деталь1.XLAT_-_D9
  N3: Arduino1.D10_PWM/SS, Деталь1.BLANK_-_D10
  N4: Arduino1.D11_PWM/MOSI, Деталь1.SIN_-_D11
  N5: Arduino1.D12/MISO, Деталь1.D12
  N6: Arduino1.D13/SCK, Деталь1.SCLK_-_D13
  GND: Arduino1.GND, Деталь1.GND, Деталь1.GND_-_GND@2
  N7: Arduino1.AREF, Деталь1.AREF
  N8: Arduino1.D3_PWM, Деталь1.GSCLK_-_D3

notes:
  BLINK

// code stored in the sketch: Blink.ino
/*
  Blink
  
  Switching a LED on and off
  
  This example is part of the Fritzing Creator Kit: www.fritzing.org/creator-kit.
*/

int led = 13;                   // integer variable led is declared

void setup() {                  // the setup() method is executed only once
  pinMode(led, OUTPUT);         // the led PIN is declared as digital output
}

void loop() {                   // the loop() method is repeated
  digitalWrite(led, HIGH);      // switching on the led 
  delay(1000);                  // stopping the program for 1000 milliseconds
  digitalWrite(led, LOW);       // switching off the led 
  delay(1000);                  // stopping the program for 1000 milliseconds
}
